# Fritzing sketch ardu_pump (saved by Fritzing 0.9.3b)
circuit board: 4cm x 3.5cm
breadboards: 1

parts:
  U2 = attiny85 [package=dip]
  J1 = female pin header, 4 pins [form="♀ (female)"]
  R1 = Resistor [tolerance=±5% resistance=220 package=THT]
  D1 = Rectifier Diode [part_number=1N4001 package="300 mil [THT]"]
  J3 = male pin header, 6 pins [form="♂ (male)"]
  REL = female pin header, 4 pins [form="♀ (female)"]
  Q1 = NPN-Transistor [package="TO92 [THT]"]
  L1 = LED - 3mm [color="Red (633nm)" package="3 mm [THT]"]
  J6 = female pin header, 2 pins [form="♀ (female)"]
  J5 = male pin header, 1 pin [form="♂ (male)"]
  J4 = male pin header, 1 pin [form="♂ (male)"]

nets:
  RST: U2.Pin_1, J3.pin3
  N1: U2.Pin_2, J1.pin2
  N2: U2.Pin_3, J1.pin3
  GND: U2.Pin_4, J1.pin4, J3.pin2, Q1.E, J6.pin2
  MOSI: U2.Pin_5, J3.pin5, L1.anode
  MISO: U2.Pin_6, J3.pin6
  SCK: U2.Pin_7, J3.pin4
  5V: U2.Pin_8, J1.pin1, D1.cathode, J3.pin1, REL.pin2, J6.pin1
  N3: R1.Pin_0, L1.cathode
  N4: R1.Pin_1, Q1.B
  N5: D1.anode, REL.pin3, Q1.C
  N6: REL.pin1, J4.pin1
  N7: REL.pin4, J5.pin1
